# Fritzing sketch circuito01 (saved by Fritzing 1.0.5)

parts:
  LED_rojo = LED - 5mm [color="Red (633nm)" current=0.030A package="5 mm [THT]"]
  U1 = LIPO-1000mAh [package=lipo-1000]
  U2 = LIPO-1000mAh [package=lipo-1000]
  part = Resistor [tolerance=±5% power=0.25W resistance=220 package=THT]

nets:
  N1: LED_rojo.cathode, U1.-
  N2: LED_rojo.anode, part.Pin_0
  N3: U1.+, U2.-
  N4: U2.+, part.Pin_1
